// Logisim project dinoGame.circ as structural Verilog: 2 circuits, main circuit main
module main (
  input  [7:0] in_1,
  input  [7:0] in_2,
  input  in_3,
  input  in_4,
  input  [7:0] in_5,
  input  [7:0] in_6,
  input  [7:0] in_7,
  input  [7:0] in_8,
  input  [7:0] in_9,
  input  [7:0] in_10,
  input  [7:0] in_11,
  input  [7:0] in_12
);

  wire [7:0] abc_1_out_5, abc_1_out_6, abc_1_out_7, abc_1_out_8, abc_1_out_9, abc_1_out_10, abc_1_out_11,
       abc_1_out_12;

  DotMatrix #(.matrixcols(8), .matrixrows(8)) dotmatrix_1 (
    .col0(in_5), .col1(in_5), .col2(in_6), .col3(in_10), .col4(in_7), .col5(in_11), .col6(in_8), .col7(in_12));
  Random random_1 ();  // open: clk, next, out, clr
  DotMatrix #(.matrixcols(8), .matrixrows(8)) dotmatrix_2 (
    .col0(abc_1_out_7), .col1(abc_1_out_8), .col2(abc_1_out_9), .col3(abc_1_out_10), .col4(abc_1_out_5),
    .col5(abc_1_out_11), .col6(abc_1_out_6), .col7(abc_1_out_12));
  ABC abc_1 (
    .\input (in_2), .start(in_3), .clock(in_4), .out_7(abc_1_out_7), .out_8(abc_1_out_8),
    .out_9(abc_1_out_9), .out_10(abc_1_out_10), .out_5(abc_1_out_5), .out_11(abc_1_out_11),
    .out_6(abc_1_out_6), .out_12(abc_1_out_12));  // open: reset

  assign in_9 = in_5;
endmodule

module ABC (
  input  [7:0] \input ,
  input  start,
  input  clock,
  input  reset,
  output [7:0] out_5,
  output [7:0] out_6,
  output [7:0] out_7,
  output [7:0] out_8,
  output [7:0] out_9,
  output [7:0] out_10,
  output [7:0] out_11,
  output [7:0] out_12
);

  Register register_1 (.D(\input ), .en(start), .Q(out_7), .clk(clock), .clr(reset));
  Register register_2 (.D(out_7), .en(start), .Q(out_8), .clk(clock), .clr(reset));
  Register register_3 (.D(out_8), .en(start), .Q(out_9), .clk(clock), .clr(reset));
  Register register_4 (.D(out_9), .Q(out_10), .clk(clock), .clr(reset));  // open: en
  Register register_5 (.D(out_10), .en(start), .Q(out_5), .clk(clock), .clr(reset));
  Register register_6 (.D(out_5), .en(start), .Q(out_11), .clk(clock), .clr(reset));
  Register register_7 (.D(out_11), .en(start), .Q(out_6), .clk(clock), .clr(reset));
  Register register_8 (.D(out_6), .en(start), .Q(out_12), .clk(clock), .clr(reset));
endmodule
