// Logisim project jump32.circ as structural Verilog: 1 circuit, main circuit jump32
module jump32 (
  input  isJump,
  input  start,
  input  clock,
  input  [31:0] character1,
  input  [31:0] character2,
  input  [31:0] character3,
  input  [31:0] character4,
  output [31:0] out_8,
  output [31:0] out_9,
  output [31:0] out_10,
  output [31:0] out_11
);

  wire and_1_out, counter_1_carry, not_1_out, not_2_out;
  wire [1:0] counter_1_q;
  wire [4:0] multiplexer_1_out;

  not not_1 (not_1_out, counter_1_carry);
  not not_2 (not_2_out, isJump);
  and and_1 (and_1_out, clock, not_1_out);
  Counter #(.width(2), .max('h3)) counter_1 (
    .load(not_2_out), .Q(counter_1_q), .carry(counter_1_carry), .clk(and_1_out));  // open: D, count, clr
  Multiplexer #(.select(2), .width(5)) multiplexer_1 (
    .in0(5'b00100), .in1(5'b00111), .in2(5'b01001), .in3(5'b01010), .out(multiplexer_1_out),
    .sel(counter_1_q), .en(start));
  Shifter #(.width(32)) shifter_1 (.in(character1), .\dist (multiplexer_1_out), .out(out_8));
  Shifter #(.width(32)) shifter_2 (.in(character2), .\dist (multiplexer_1_out), .out(out_9));
  Shifter #(.width(32)) shifter_3 (.in(character3), .\dist (multiplexer_1_out), .out(out_10));
  Shifter #(.width(32)) shifter_4 (.in(character4), .\dist (multiplexer_1_out), .out(out_11));

  // Notes on the sheet:
  //   animation frame
  //   character
  //   distance
  //   output_character
endmodule
