// Logisim project test.circ as structural Verilog: 1 circuit, main circuit main
module main (
  input  [31:0] in_1,
  input  [31:0] in_2,
  input  [31:0] in_3,
  input  [31:0] in_4,
  input  [31:0] in_5,
  input  [31:0] in_6,
  input  start,
  input  reset,
  input  isMake,
  input  [7:0] delayTime,
  input  start_2,
  output \output 
);

  wire clock_2_out, clock_out, counter_1_carry, not_1_out, or_1_out, register_1_q;
  wire [31:0] bumpincoder32_1_display1, bumpincoder32_1_display2, bumpincoder32_1_display3,
       bumpincoder32_1_display4, bumpincoder32_1_display5, bumpincoder32_1_display6,
       bumpincoder32_1_display7, bumpincoder32_1_display8, bumpincoder32_1_display9,
       bumpincoder32_1_display10, bumpincoder32_1_display11, bumpincoder32_1_display12,
       bumpincoder32_1_display13, bumpincoder32_1_display14, bumpincoder32_1_display15,
       bumpincoder32_1_display16, bumpincoder32_1_display17, bumpincoder32_1_display18,
       bumpincoder32_1_display19, bumpincoder32_1_display20, bumpincoder32_1_display21,
       bumpincoder32_1_display22, bumpincoder32_1_display23, bumpincoder32_1_display24,
       bumpincoder32_1_display25, bumpincoder32_1_display26, bumpincoder32_1_display27,
       bumpincoder32_1_display28, bumpincoder32_1_display29, bumpincoder32_1_display30,
       bumpincoder32_1_display31, bumpincoder32_1_display32, pushbump32_1_output;

  Clock clock (.out(clock_out));
  or or_1 (or_1_out, isMake, \output );
  Clock clock_2 (.out(clock_2_out));
  not not_1 (not_1_out, \output );
  pushBump32 pushbump32_1 (
    .start(start), .clock(clock_out), .reset(reset), .making(or_1_out), .empty_block(in_1), .block5(in_2),
    .block4(in_3), .block3(in_4), .block2(in_5), .block1(in_6), .\output (pushbump32_1_output));
  Counter counter_1 (
    .load(start_2), .D(delayTime), .count(not_1_out), .carry(counter_1_carry), .clk(clock_2_out),
    .clr(register_1_q));  // open: Q
  Register #(.width(1)) register_1 (
    .D(counter_1_carry), .en(start_2), .Q(register_1_q), .clk(clock_2_out));  // open: clr
  Register #(.width(1)) register_2 (.D(register_1_q), .en(start_2), .Q(\output ), .clk(clock_2_out));  // open: clr
  DotMatrix #(.matrixcols(32), .matrixrows(32)) dotmatrix_1 (
    .col0(bumpincoder32_1_display1), .col1(bumpincoder32_1_display2), .col2(bumpincoder32_1_display3),
    .col3(bumpincoder32_1_display4), .col4(bumpincoder32_1_display5), .col5(bumpincoder32_1_display6),
    .col6(bumpincoder32_1_display7), .col7(bumpincoder32_1_display8), .col8(bumpincoder32_1_display9),
    .col9(bumpincoder32_1_display10), .col10(bumpincoder32_1_display11), .col11(bumpincoder32_1_display12),
    .col12(bumpincoder32_1_display13), .col13(bumpincoder32_1_display14), .col14(bumpincoder32_1_display15),
    .col15(bumpincoder32_1_display16), .col16(bumpincoder32_1_display17), .col17(bumpincoder32_1_display18),
    .col18(bumpincoder32_1_display19), .col19(bumpincoder32_1_display20), .col20(bumpincoder32_1_display21),
    .col21(bumpincoder32_1_display22), .col22(bumpincoder32_1_display23), .col23(bumpincoder32_1_display24),
    .col24(bumpincoder32_1_display25), .col25(bumpincoder32_1_display26), .col26(bumpincoder32_1_display27),
    .col27(bumpincoder32_1_display28), .col28(bumpincoder32_1_display29), .col29(bumpincoder32_1_display30),
    .col30(bumpincoder32_1_display31), .col31(bumpincoder32_1_display32));
  bumpIncoder32 bumpincoder32_1 (
    .start_data(pushbump32_1_output), .start(start), .clock(clock_out), .reset(reset),
    .display1(bumpincoder32_1_display1), .display2(bumpincoder32_1_display2),
    .display3(bumpincoder32_1_display3), .display4(bumpincoder32_1_display4),
    .display5(bumpincoder32_1_display5), .display6(bumpincoder32_1_display6),
    .display7(bumpincoder32_1_display7), .display8(bumpincoder32_1_display8),
    .display9(bumpincoder32_1_display9), .display10(bumpincoder32_1_display10),
    .display11(bumpincoder32_1_display11), .display12(bumpincoder32_1_display12),
    .display13(bumpincoder32_1_display13), .display14(bumpincoder32_1_display14),
    .display15(bumpincoder32_1_display15), .display16(bumpincoder32_1_display16),
    .display17(bumpincoder32_1_display17), .display18(bumpincoder32_1_display18),
    .display19(bumpincoder32_1_display19), .display20(bumpincoder32_1_display20),
    .display21(bumpincoder32_1_display21), .display22(bumpincoder32_1_display22),
    .display23(bumpincoder32_1_display23), .display24(bumpincoder32_1_display24),
    .display25(bumpincoder32_1_display25), .display26(bumpincoder32_1_display26),
    .display27(bumpincoder32_1_display27), .display28(bumpincoder32_1_display28),
    .display29(bumpincoder32_1_display29), .display30(bumpincoder32_1_display30),
    .display31(bumpincoder32_1_display31), .display32(bumpincoder32_1_display32));  // open: character1, character2, character3, character4, isBumped, final_data, start_output, clock_output, reset_output
endmodule
